// Logisim project 1.circ as structural Verilog: 1 circuit, main circuit main
module main (
  input  A,
  input  B,
  input  C,
  output B_2,
  output C_out
);

  wire and_1_out, and_2_out, or_1_out;

  or or_1 (or_1_out, A, B);
  and and_1 (and_1_out, A, B);
  or or_2 (B_2, or_1_out, C);
  and and_2 (and_2_out, or_1_out, C);
  or or_3 (C_out, and_2_out, and_1_out);
endmodule
