// Logisim project D Latch.circ as structural Verilog: 1 circuit, main circuit main
module main (
  input  D,
  input  Strobe
);

  wire not_1_out;

  not not_1 (not_1_out, D);
  // AND_Gate and_1 has open pins: in0=D, in4=Strobe, out=open
  // AND_Gate and_2 has open pins: in0=not_1_out, in4=Strobe, out=open
endmodule
