// Logisim project circuits.circ as structural Verilog: 3 circuits, main circuit MyXOR
module MyXOR (
  input  X,
  input  Y,
  output Output
);

  wire and_1_out, and_2_out, not_1_out, not_2_out;

  not not_1 (not_1_out, Y);
  not not_2 (not_2_out, X);
  and and_1 (and_1_out, X, not_1_out);
  and and_2 (and_2_out, not_2_out, Y);
  or or_1 (Output, and_1_out, and_2_out);

  // Notes on the sheet:
  //   Here is a location to build an XOR circuit
  //   We already implemented this circuit in class.  Copy it here.
endmodule

module FullAdder (
  input  X,
  input  Y,
  input  CarryIn,
  input  X_2,
  input  Y_2,
  output sum,
  output CarryOut
);

  wire and_1_out, and_2_out, and_3_out, and_4_out, and_5_out, and_6_out, and_7_out, and_8_out, not_1_out,
       not_2_out, not_3_out, not_4_out, not_5_out, not_6_out, or_1_out;

  and and_1 (and_1_out, X, Y);
  not not_1 (not_1_out, Y);
  and and_2 (and_2_out, X, not_1_out);
  or or_1 (or_1_out, and_2_out, and_5_out);
  not not_2 (not_2_out, or_1_out);
  and and_3 (and_3_out, not_2_out, CarryIn);
  and and_4 (and_4_out, or_1_out, CarryIn);
  or or_2 (CarryOut, and_1_out, and_4_out);
  not not_3 (not_3_out, X);
  and and_5 (and_5_out, not_3_out, Y);
  or or_3 (sum, and_3_out, and_6_out);
  not not_4 (not_4_out, Y_2);
  not not_5 (not_5_out, X_2);
  not not_6 (not_6_out, CarryIn);
  and and_6 (and_6_out, or_1_out, not_6_out);
  and and_7 (and_7_out, X_2, not_4_out);
  and and_8 (and_8_out, not_5_out, Y_2);
  // OR_Gate or_4 has open pins: in1=and_7_out, in3=and_8_out, out=open
endmodule

module _4_bit_Ripple_Carry_Adder (
  input  Y3,
  input  Y2,
  input  Y1,
  input  Y0,
  input  X3,
  input  X2,
  input  X1,
  input  X0,
  output Sum4,
  output Sum3,
  output Sum2,
  output Sum1,
  output Sum0
);

  wire fulladder_2_carryout, fulladder_3_carryout, fulladder_4_carryout;

  FullAdder fulladder_1 (
    .X(X3), .Y(Y3), .CarryIn(fulladder_2_carryout), .sum(Sum3), .CarryOut(Sum4));  // open: X_2, Y_2
  FullAdder fulladder_2 (
    .X(X2), .Y(Y2), .CarryIn(fulladder_3_carryout), .sum(Sum2), .CarryOut(fulladder_2_carryout));  // open: X_2, Y_2
  FullAdder fulladder_3 (
    .X(X1), .Y(Y1), .CarryIn(fulladder_4_carryout), .sum(Sum1), .CarryOut(fulladder_3_carryout));  // open: X_2, Y_2
  FullAdder fulladder_4 (
    .X(X0), .Y(Y0), .CarryIn(1'b0), .sum(Sum0), .CarryOut(fulladder_4_carryout));  // open: X_2, Y_2
endmodule
