// Logisim project cs115.circ as structural Verilog: 3 circuits, main circuit S-R Latch
module main (
  input  A,
  input  B,
  input  C,
  output S,
  output C_out
);

  wire and_1_out, and_2_out, xor_1_out;

  xor xor_1 (xor_1_out, A, B);
  and and_1 (and_1_out, A, B);
  xor xor_2 (S, xor_1_out, C);
  and and_2 (and_2_out, xor_1_out, C);
  or or_1 (C_out, and_2_out, and_1_out);
endmodule

module S_R_Latch (
  input  S,
  input  R,
  output not_Q,
  output Q
);

  wire or_1_out, or_2_out;

  or or_1 (or_1_out, S, Q);
  or or_2 (or_2_out, not_Q, R);
  not not_1 (not_Q, or_1_out);
  not not_2 (Q, or_2_out);
endmodule

module D_Latch (
  input  D,
  input  Strobe,
  output out_3,
  output out_4
);

  wire and_1_out, and_2_out, not_1_out;

  not not_1 (not_1_out, D);
  and and_1 (and_1_out, D, Strobe);
  and and_2 (and_2_out, not_1_out, Strobe);
  S_R_Latch s_r_latch_1 (.S(and_1_out), .R(and_2_out), .not_Q(out_3), .Q(out_4));
endmodule
